// Logisim project cheat.circ as structural Verilog: 2 circuits, main circuit main
module main (
  input  in_1,
  input  in_2,
  output out_3
);

  wire clock_1_out;
  wire [6:0] keyboard_1_data;

  Clock clock_1 (.out(clock_1_out));
  Keyboard keyboard_1 (.clk(clock_1_out), .clr(in_2), .data(keyboard_1_data));  // open: re, avail
  FSM fsm_1 (.in_1(keyboard_1_data), .in_2(clock_1_out), .in_3(in_1), .out_4(out_3));
endmodule

module FSM (
  input  [6:0] in_1,
  input  in_2,
  input  in_3,
  output out_4
);

  wire _0_q, _0_qn, _1_q, _1_qn, and_1_out, and_2_out, and_3_out, and_4_out, and_5_out, not_1_out, or_1_out,
       or_2_out;

  D_Flip_Flop _1 (.clk(in_2), .D(or_1_out), .Q(_1_q), .Qn(_1_qn), .reset(in_3));  // open: preset, en
  D_Flip_Flop _0 (.clk(in_2), .D(or_2_out), .Q(_0_q), .Qn(_0_qn), .reset(in_3));  // open: preset, en
  not not_1 (not_1_out, in_1[2]);
  and and_1 (and_1_out, in_1[1], in_1[2], _0_q, _1_qn);
  and and_2 (and_2_out, in_1[1], _1_q, _0_qn);
  and and_3 (and_3_out, _1_qn, _0_qn, in_1[1], in_1[2]);
  and and_4 (and_4_out, _1_q, _0_q, in_1[1], in_1[2]);
  and and_5 (and_5_out, _1_q, _0_qn, not_1_out, in_1[1]);
  or or_1 (or_1_out, and_1_out, and_2_out);
  or or_2 (or_2_out, and_3_out, and_4_out, and_5_out);
  and and_6 (out_4, _1_q, _0_q);
endmodule
