// Logisim project clock.circ as structural Verilog: 6 circuits, main circuit main
module main (
  input  in_1
);

  wire bcd2ssd_1_a, bcd2ssd_1_b, bcd2ssd_1_c, bcd2ssd_1_d, bcd2ssd_1_e, bcd2ssd_1_f, bcd2ssd_1_g,
       bcd2ssd_2_a, bcd2ssd_2_b, bcd2ssd_2_c, bcd2ssd_2_d, bcd2ssd_2_e, bcd2ssd_2_f, bcd2ssd_2_g,
       bcd2ssd_3_a, bcd2ssd_3_b, bcd2ssd_3_c, bcd2ssd_3_d, bcd2ssd_3_e, bcd2ssd_3_f, bcd2ssd_3_g,
       bcd2ssd_4_a, bcd2ssd_4_b, bcd2ssd_4_c, bcd2ssd_4_d, bcd2ssd_4_e, bcd2ssd_4_f, bcd2ssd_4_g,
       clock_1_out, zerar0_2_1_out_4, zerar0_2_1_out_5, zerar0_6_1_out_3, zerar0_9_1_out_3;
  wire [3:0] contador_1_out_3, contador_2_out_3, contador_3_out_3, contador_4_out_3;

  _7_Segment_Display u_7_segment_display_1 (
    .g(bcd2ssd_1_g), .f(bcd2ssd_1_f), .a(bcd2ssd_1_a), .b(bcd2ssd_1_b), .e(bcd2ssd_1_e), .d(bcd2ssd_1_d),
    .c(bcd2ssd_1_c));  // open: dp
  bcd2ssd bcd2ssd_1 (
    .in_1(contador_1_out_3), .a(bcd2ssd_1_a), .b(bcd2ssd_1_b), .c(bcd2ssd_1_c), .d(bcd2ssd_1_d),
    .e(bcd2ssd_1_e), .f(bcd2ssd_1_f), .g(bcd2ssd_1_g));
  zerar0_2 zerar0_2_1 (
    .in_1(contador_1_out_3), .in_2(in_1), .in_3(contador_2_out_3), .out_4(zerar0_2_1_out_4),
    .out_5(zerar0_2_1_out_5));
  contador contador_1 (.in_1(zerar0_2_1_out_5), .in_2(zerar0_2_1_out_4), .out_3(contador_1_out_3));
  contador contador_2 (.in_1(zerar0_6_1_out_3), .in_2(zerar0_2_1_out_5), .out_3(contador_2_out_3));
  _7_Segment_Display u_7_segment_display_2 (
    .g(bcd2ssd_2_g), .f(bcd2ssd_2_f), .a(bcd2ssd_2_a), .b(bcd2ssd_2_b), .e(bcd2ssd_2_e), .d(bcd2ssd_2_d),
    .c(bcd2ssd_2_c));  // open: dp
  bcd2ssd bcd2ssd_2 (
    .in_1(contador_2_out_3), .a(bcd2ssd_2_a), .b(bcd2ssd_2_b), .c(bcd2ssd_2_c), .d(bcd2ssd_2_d),
    .e(bcd2ssd_2_e), .f(bcd2ssd_2_f), .g(bcd2ssd_2_g));
  LED led_1 (.in(clock_1_out));
  LED led_2 (.in(clock_1_out));
  _7_Segment_Display u_7_segment_display_3 (
    .g(bcd2ssd_3_g), .f(bcd2ssd_3_f), .a(bcd2ssd_3_a), .b(bcd2ssd_3_b), .e(bcd2ssd_3_e), .d(bcd2ssd_3_d),
    .c(bcd2ssd_3_c));  // open: dp
  bcd2ssd bcd2ssd_3 (
    .in_1(contador_3_out_3), .a(bcd2ssd_3_a), .b(bcd2ssd_3_b), .c(bcd2ssd_3_c), .d(bcd2ssd_3_d),
    .e(bcd2ssd_3_e), .f(bcd2ssd_3_f), .g(bcd2ssd_3_g));
  contador contador_3 (.in_1(zerar0_9_1_out_3), .in_2(zerar0_6_1_out_3), .out_3(contador_3_out_3));
  zerar0_6 zerar0_6_1 (.in_1(contador_3_out_3), .in_2(in_1), .out_3(zerar0_6_1_out_3));
  contador contador_4 (.in_1(clock_1_out), .in_2(zerar0_9_1_out_3), .out_3(contador_4_out_3));
  Clock clock_1 (.out(clock_1_out));
  _7_Segment_Display u_7_segment_display_4 (
    .g(bcd2ssd_4_g), .f(bcd2ssd_4_f), .a(bcd2ssd_4_a), .b(bcd2ssd_4_b), .e(bcd2ssd_4_e), .d(bcd2ssd_4_d),
    .c(bcd2ssd_4_c));  // open: dp
  bcd2ssd bcd2ssd_4 (
    .in_1(contador_4_out_3), .a(bcd2ssd_4_a), .b(bcd2ssd_4_b), .c(bcd2ssd_4_c), .d(bcd2ssd_4_d),
    .e(bcd2ssd_4_e), .f(bcd2ssd_4_f), .g(bcd2ssd_4_g));
  zerar0_9 zerar0_9_1 (.in_1(contador_4_out_3), .in_2(in_1), .out_3(zerar0_9_1_out_3));
  // Probe on contador_4_out_3
endmodule

module contador (
  input  in_1,
  input  in_2,
  output [3:0] out_3
);

  wire d_ff_1_qn, d_ff_2_qn, d_ff_3_qn, d_ff_4_qn;

  D_Flip_Flop d_ff_1 (.clk(in_1), .D(d_ff_1_qn), .Q(out_3[0]), .Qn(d_ff_1_qn), .reset(in_2));  // open: preset, en
  D_Flip_Flop d_ff_2 (.clk(d_ff_1_qn), .D(d_ff_2_qn), .Q(out_3[1]), .Qn(d_ff_2_qn), .reset(in_2));  // open: preset, en
  D_Flip_Flop d_ff_3 (.clk(d_ff_2_qn), .D(d_ff_3_qn), .Q(out_3[2]), .Qn(d_ff_3_qn), .reset(in_2));  // open: preset, en
  D_Flip_Flop d_ff_4 (.clk(d_ff_3_qn), .D(d_ff_4_qn), .Q(out_3[3]), .Qn(d_ff_4_qn), .reset(in_2));  // open: preset, en
endmodule

module zerar0_9 (
  input  [3:0] in_1,
  input  in_2,
  output out_3
);

  wire and_1_out, not_1_out, not_2_out;

  not not_1 (not_1_out, in_1[0]);
  not not_2 (not_2_out, in_1[2]);
  and and_1 (and_1_out, not_1_out, in_1[1], not_2_out, in_1[3]);
  or or_1 (out_3, and_1_out, in_2);
endmodule

module zerar0_6 (
  input  [3:0] in_1,
  input  in_2,
  output out_3
);

  wire and_1_out, not_1_out, not_2_out;

  not not_1 (not_1_out, in_1[0]);
  not not_2 (not_2_out, in_1[3]);
  and and_1 (and_1_out, not_1_out, in_1[1], in_1[2], not_2_out);
  or or_1 (out_3, and_1_out, in_2);
endmodule

module bcd2ssd (
  input  [3:0] in_1,
  output a,
  output b,
  output c,
  output d,
  output e,
  output f,
  output g
);

  wire and_1_out, and_2_out, and_3_out, and_4_out, and_5_out, and_6_out, and_7_out, and_8_out, and_9_out,
       and_10_out, and_11_out, and_12_out, and_13_out, and_14_out, and_15_out, and_16_out, not_1_out,
       not_2_out, not_3_out, not_4_out, not_5_out, not_6_out, not_7_out, not_8_out, not_9_out, not_10_out,
       not_11_out, not_12_out, not_13_out, not_14_out, not_15_out, not_16_out, not_17_out, not_18_out,
       not_19_out, not_20_out, not_21_out;

  not not_1 (not_1_out, in_1[2]);
  not not_2 (not_2_out, in_1[0]);
  not not_3 (not_3_out, in_1[1]);
  not not_4 (not_4_out, in_1[0]);
  not not_5 (not_5_out, in_1[1]);
  not not_6 (not_6_out, in_1[2]);
  not not_7 (not_7_out, in_1[0]);
  not not_8 (not_8_out, in_1[2]);
  not not_9 (not_9_out, in_1[0]);
  not not_10 (not_10_out, in_1[1]);
  not not_11 (not_11_out, in_1[2]);
  not not_12 (not_12_out, in_1[0]);
  not not_13 (not_13_out, in_1[0]);
  not not_14 (not_14_out, in_1[1]);
  not not_15 (not_15_out, in_1[0]);
  not not_16 (not_16_out, in_1[1]);
  not not_17 (not_17_out, in_1[0]);
  not not_18 (not_18_out, in_1[2]);
  not not_19 (not_19_out, in_1[1]);
  not not_20 (not_20_out, in_1[0]);
  and and_1 (and_1_out, not_1_out, not_2_out);
  and and_2 (and_2_out, in_1[2], in_1[0]);
  not not_21 (not_21_out, in_1[2]);
  and and_3 (and_3_out, not_3_out, not_4_out);
  and and_4 (and_4_out, in_1[1], in_1[0]);
  or or_1 (c, not_5_out, in_1[0], in_1[2]);
  and and_5 (and_5_out, not_6_out, not_7_out);
  and and_6 (and_6_out, not_8_out, in_1[1]);
  and and_7 (and_7_out, in_1[1], not_9_out);
  and and_8 (and_8_out, in_1[2], not_10_out, in_1[0]);
  and and_9 (and_9_out, not_11_out, not_12_out);
  and and_10 (and_10_out, in_1[1], not_13_out);
  and and_11 (and_11_out, not_14_out, not_15_out);
  and and_12 (and_12_out, in_1[2], not_16_out);
  and and_13 (and_13_out, in_1[2], not_17_out);
  and and_14 (and_14_out, not_18_out, in_1[1]);
  and and_15 (and_15_out, in_1[2], not_19_out);
  and and_16 (and_16_out, in_1[2], not_20_out);
  or or_2 (a, and_1_out, in_1[1], and_2_out, in_1[3]);
  or or_3 (b, not_21_out, and_3_out, and_4_out);
  or or_4 (d, and_5_out, and_6_out, and_7_out, and_8_out, in_1[3]);
  or or_5 (e, and_9_out, and_10_out);
  or or_6 (f, and_11_out, and_12_out, and_13_out, in_1[3]);
  or or_7 (g, and_14_out, and_15_out, and_16_out, in_1[3]);
endmodule

module zerar0_2 (
  input  [3:0] in_1,
  input  in_2,
  input  [3:0] in_3,
  output out_4,
  output out_5
);

  wire and_1_out, and_2_out, and_3_out, and_4_out, not_1_out, not_2_out, not_3_out, not_4_out, not_5_out,
       not_6_out, not_7_out, not_8_out, or_1_out;

  not not_1 (not_1_out, in_1[3]);
  not not_2 (not_2_out, in_1[2]);
  not not_3 (not_3_out, in_1[0]);
  not not_4 (not_4_out, in_3[3]);
  not not_5 (not_5_out, in_3[1]);
  not not_6 (not_6_out, in_3[0]);
  not not_7 (not_7_out, in_3[0]);
  and and_1 (and_1_out, not_7_out, in_3[1], not_8_out, in_3[3]);
  not not_8 (not_8_out, in_3[2]);
  and and_2 (and_2_out, not_1_out, not_2_out, in_1[1], not_3_out);
  and and_3 (and_3_out, not_4_out, in_3[2], not_5_out, not_6_out);
  or or_1 (or_1_out, in_2, and_1_out);
  and and_4 (and_4_out, and_2_out, and_3_out);
  or or_2 (out_4, and_4_out, in_2);
  or or_3 (out_5, out_4, or_1_out);
endmodule
