// Logisim project contador-síncrono-modular.circ as structural Verilog: 1 circuit, main circuit main
module main (
);

  wire and_1_out, and_2_out, clock_1_out, t_ff_1_q, t_ff_2_q, t_ff_3_q, t_ff_4_q;

  Clock clock_1 (.out(clock_1_out));
  T_Flip_Flop t_ff_1 (.clk(clock_1_out), .T(1'b1), .Q(t_ff_1_q));  // open: Qn, preset, reset, en
  T_Flip_Flop t_ff_2 (.clk(clock_1_out), .T(t_ff_1_q), .Q(t_ff_2_q));  // open: Qn, preset, reset, en
  and and_1 (and_1_out, t_ff_2_q, t_ff_1_q);
  T_Flip_Flop t_ff_3 (.clk(clock_1_out), .T(and_1_out), .Q(t_ff_3_q));  // open: Qn, preset, reset, en
  T_Flip_Flop t_ff_4 (.clk(clock_1_out), .T(and_2_out), .Q(t_ff_4_q));  // open: Qn, preset, reset, en
  and and_2 (and_2_out, t_ff_3_q, and_1_out);

  // Notes on the sheet:
  //   Contador sincrono (blocos modulares)
endmodule
