// Logisim project joystic-contador.circ as structural Verilog: 3 circuits, main circuit main
module main (
  input  [9:0] in_1,
  input  in_2
);

  wire clock_1_out, comparador_1_out_3;
  wire [2:0] joystick_1_y;
  wire [9:0] adder_1_out, conversor_1_out_2, register_1_q;

  Joystick #(.bits(3)) joystick_1 (.y(joystick_1_y));  // open: x
  // Probe on joystick_1_y
  // Probe on conversor_1_out_2
  conversor conversor_1 (.in_1(joystick_1_y), .out_2(conversor_1_out_2));
  Adder #(.width(10)) adder_1 (.a(conversor_1_out_2), .b(register_1_q), .out(adder_1_out), .cin(1'b0));  // open: cout
  // Probe on adder_1_out
  comparador comparador_1 (.in_1(adder_1_out), .in_2(in_1), .out_3(comparador_1_out_3));
  Register #(.width(10)) register_1 (
    .D(adder_1_out), .en(comparador_1_out_3), .Q(register_1_q), .clk(clock_1_out), .clr(in_2));
  Clock clock_1 (.out(clock_1_out));
  // Probe on register_1_q
endmodule

module conversor (
  input  [2:0] in_1,
  output [9:0] out_2
);

  wire and_1_out, and_2_out, and_3_out, and_4_out, and_5_out, and_6_out, and_7_out, and_8_out, and_9_out,
       and_10_out, and_11_out, and_12_out, and_13_out, and_14_out, and_15_out, and_16_out, and_17_out,
       and_18_out, not_1_out, not_2_out, not_3_out, not_4_out, not_5_out;

  and and_1 (and_1_out, in_1[2], in_1[0]);
  and and_2 (and_2_out, in_1[2], in_1[1]);
  and and_3 (and_3_out, in_1[2], in_1[0]);
  and and_4 (and_4_out, in_1[2], in_1[1]);
  and and_5 (and_5_out, in_1[2], in_1[0]);
  and and_6 (and_6_out, in_1[2], in_1[1]);
  and and_7 (and_7_out, in_1[2], in_1[0]);
  and and_8 (and_8_out, in_1[2], in_1[1]);
  and and_9 (and_9_out, in_1[2], in_1[0]);
  and and_10 (and_10_out, in_1[2], in_1[1]);
  and and_11 (and_11_out, in_1[2], in_1[0]);
  and and_12 (and_12_out, in_1[2], in_1[1]);
  not not_1 (not_1_out, in_1[2]);
  not not_2 (not_2_out, in_1[1]);
  not not_3 (not_3_out, in_1[2]);
  not not_4 (not_4_out, in_1[0]);
  not not_5 (not_5_out, in_1[1]);
  or or_1 (out_2[9], and_1_out, and_2_out);
  or or_2 (out_2[8], and_3_out, and_4_out);
  or or_3 (out_2[7], and_5_out, and_6_out);
  or or_4 (out_2[6], and_7_out, and_8_out);
  or or_5 (out_2[5], and_9_out, and_10_out);
  or or_6 (out_2[4], and_11_out, and_12_out);
  and and_13 (and_13_out, not_1_out, not_2_out, in_1[0]);
  and and_14 (and_14_out, in_1[2], in_1[1]);
  and and_15 (and_15_out, not_3_out, in_1[1], not_4_out);
  and and_16 (and_16_out, in_1[2], in_1[0]);
  and and_17 (and_17_out, not_5_out, in_1[0]);
  and and_18 (and_18_out, in_1[2], in_1[1]);
  or or_7 (out_2[3], and_13_out, and_14_out);
  or or_8 (out_2[2], and_15_out, and_16_out);
  or or_9 (out_2[1], and_17_out, and_18_out);

  assign out_2[0] = in_1[1];
endmodule

module comparador (
  input  [9:0] in_1,
  input  [9:0] in_2,
  output out_3
);

  wire comparator_1_gt, comparator_2_lt, not_1_out, not_2_out;

  Comparator #(.width(10)) comparator_1 (.a(in_1), .b(in_2), .gt(comparator_1_gt));  // open: eq, lt
  not not_1 (not_1_out, comparator_1_gt);
  Comparator #(.width(10)) comparator_2 (.a(in_1), .b({10{1'b0}}), .lt(comparator_2_lt));  // open: gt, eq
  not not_2 (not_2_out, comparator_2_lt);
  and and_1 (out_3, not_1_out, not_2_out);
endmodule
