// Logisim project lab_especial.circ as structural Verilog: 5 circuits, main circuit main
module main (
);

  wire botao_out, clock_1_out, contador_1_out_3, contador_2_out_3, keyboard_1_avail, limite_out, or_1_out;
  wire [1:0] register_2_q;
  wire [3:0] _0_q, contador_1_out_2, contador_2_out_2, register_3_q, register_4_q;
  wire [6:0] keyboard_1_data, rom_1_data;
  wire [9:0] deslocador_1_out_3, deslocador_1_out_4;

  Clock clock_1 (.out(clock_1_out));
  Button botao (.out(botao_out));
  Register #(.width(1)) register_1 (.D(1'b1), .Q(_0_q[3]), .clk(botao_out), .clr(or_1_out));  // open: en
  Keyboard keyboard_1 (.clk(clock_1_out), .avail(keyboard_1_avail), .data(keyboard_1_data));  // open: re, clr
  D_Flip_Flop _0 (.clk(clock_1_out), .D(rom_1_data[0]), .Q(_0_q[0]), .reset(or_1_out));  // open: Qn, preset, en
  D_Flip_Flop _1 (.clk(clock_1_out), .D(rom_1_data[1]), .Q(_0_q[1]), .reset(or_1_out));  // open: Qn, preset, en
  D_Flip_Flop _2 (.clk(clock_1_out), .D(rom_1_data[2]), .Q(_0_q[2]), .reset(or_1_out));  // open: Qn, preset, en
  Register #(.width(2)) register_2 (
    .D(keyboard_1_data[2:1]), .en(keyboard_1_avail), .Q(register_2_q), .clk(clock_1_out), .clr(or_1_out));
  ROM #(.addrWidth(6), .dataWidth(7)) rom_1 (.addr({register_2_q, _0_q}), .data(rom_1_data));  // open: sel
  Register #(.width(4)) register_3 (
    .D(contador_1_out_2), .en(rom_1_data[6]), .Q(register_3_q), .clk(clock_1_out), .clr(or_1_out));
  contador contador_1 (.in_1(register_3_q), .out_2(contador_1_out_2), .out_3(contador_1_out_3));
  contador contador_2 (.in_1(register_4_q), .out_2(contador_2_out_2), .out_3(contador_2_out_3));
  Register #(.width(4)) register_4 (
    .D(contador_2_out_2), .en(rom_1_data[4]), .Q(register_4_q), .clk(clock_1_out), .clr(or_1_out));
  Button limite (.out(limite_out));
  deslocador deslocador_1 (
    .in_1(contador_1_out_2), .in_2(contador_2_out_2), .out_3(deslocador_1_out_3), .out_4(deslocador_1_out_4));
  or or_1 (or_1_out, contador_2_out_3, contador_1_out_3, limite_out);
  // DotMatrix #(.inputtype("select"), .matrixcols(10), .matrixrows(10)) dotmatrix_1: pin names not known; wires that end beside it: deslocador_1_out_3, deslocador_1_out_4

  // Notes on the sheet:
  //   w=11; a=00; s=01; d=10
  //   Problemas: Fazer subtrair o mesmo número que somar e vice versa;
  //   Fazer começar em (5,5)
  //   O registro teria que ser feito e alterado a maquina de estados na hora
  //   Registra a direção para manter
  //   contents of rom_1 (hex, n*v repeats v):
  //   0 41 22 a 12 0 0 0 1 41 22 a 12 4*0 43 23 b 14 0 0 0 1 43 23 b 14 4*0 41 22 9 11 0 0 0 1 41 22 9 11
  //   4*0 44 24 b 14 0 0 0 1 44 24 b 14
  //   soma a linha
  //   3) Quando ativado decrementaY
  //   4) Quando ativado incrementaY
  //   5) Quando ativado decrementaX
  //   6) Quando ativado incrementaX
  //   soma a coluna
  //   Aqui verifica quando chegou nos limites e zera tudo
endmodule

module maior (
  input  [3:0] in_1,
  output out_2
);

  Comparator #(.width(4)) comparator_1 (.a(in_1), .b(4'b1010), .gt(out_2));  // open: eq, lt
  // Probe on 4'b1010
endmodule

module menor (
  input  [3:0] in_1,
  output out_2
);

  Comparator #(.width(4)) comparator_1 (.a(in_1), .b(4'b0000), .lt(out_2));  // open: gt, eq
  // Probe on 4'b0000
endmodule

module deslocador (
  input  [3:0] in_1,
  input  [3:0] in_2,
  output [9:0] out_3,
  output [9:0] out_4
);

  Shifter #(.width(10)) shifter_1 (.in(10'h1), .\dist (in_1), .out(out_3));
  Shifter #(.width(10)) shifter_2 (.in(10'h1), .\dist (in_2), .out(out_4));
endmodule

module contador (
  input  [3:0] in_1,
  output [3:0] out_2,
  output out_3
);

  wire not_1_out;

  // Probe on out_2
  Adder #(.width(4)) adder_1 (.a(in_1), .b(4'b0001), .out(out_2));  // open: cin, cout
  not not_1 (not_1_out, out_2[2]);
  and and_1 (out_3, out_2[0], out_2[1], not_1_out, out_2[3]);
endmodule
