// Logisim project lab_random.circ as structural Verilog: 4 circuits, main circuit main
module main (
  input  [4:0] in_1,
  input  in_2
);

  wire clock_1_out;
  wire [4:0] registrador_1_out_4, somador_1_out_3;

  // Probe on in_1
  // Probe on registrador_1_out_4
  somador somador_1 (.in_1(registrador_1_out_4), .in_2(in_1), .out_3(somador_1_out_3));
  // Probe on somador_1_out_3
  Clock clock_1 (.out(clock_1_out));
  registrador registrador_1 (.in_1(somador_1_out_3), .in_2(clock_1_out), .in_3(in_2), .out_4(registrador_1_out_4));
endmodule

module somador (
  input  [4:0] in_1,
  input  [4:0] in_2,
  output [4:0] out_3
);

  wire adder_1_cout, adder_2_cout, adder_3_cout, adder_4_cout;

  Adder #(.width(1)) adder_1 (.a(in_2[0]), .b(in_1[0]), .out(out_3[0]), .cin(1'b0), .cout(adder_1_cout));
  Adder #(.width(1)) adder_2 (.a(in_2[1]), .b(in_1[1]), .out(out_3[1]), .cin(adder_1_cout), .cout(adder_2_cout));
  Adder #(.width(1)) adder_3 (.a(in_2[2]), .b(in_1[2]), .out(out_3[2]), .cin(adder_2_cout), .cout(adder_3_cout));
  Adder #(.width(1)) adder_4 (.a(in_2[3]), .b(in_1[3]), .out(out_3[3]), .cin(adder_3_cout), .cout(adder_4_cout));
  Adder #(.width(1)) adder_5 (.a(in_2[4]), .b(in_1[4]), .out(out_3[4]), .cin(adder_4_cout));  // open: cout
  // Probe on out_3
endmodule

module registrador (
  input  [4:0] in_1,
  input  in_2,
  input  in_3,
  output [4:0] out_4
);

  D_Flip_Flop d_ff_1 (.clk(in_2), .D(in_1[0]), .Q(out_4[0]), .reset(in_3));  // open: Qn, preset, en
  D_Flip_Flop d_ff_2 (.clk(in_2), .D(in_1[1]), .Q(out_4[1]), .reset(in_3));  // open: Qn, preset, en
  D_Flip_Flop d_ff_3 (.clk(in_2), .D(in_1[2]), .Q(out_4[2]), .reset(in_3));  // open: Qn, preset, en
  D_Flip_Flop d_ff_4 (.clk(in_2), .D(in_1[3]), .Q(out_4[3]), .reset(in_3));  // open: Qn, preset, en
  D_Flip_Flop d_ff_5 (.clk(in_2), .D(in_1[4]), .Q(out_4[4]), .reset(in_3));  // open: Qn, preset, en
endmodule

module asdasd (
  input  in_1
);

  wire clock_1_out, d_ff_1_q, d_ff_2_q, d_ff_3_q, d_ff_4_q, not_1_out;

  Clock clock_1 (.out(clock_1_out));
  D_Flip_Flop d_ff_1 (.clk(clock_1_out), .D(not_1_out), .Q(d_ff_1_q), .reset(in_1));  // open: Qn, preset, en
  D_Flip_Flop d_ff_2 (.clk(clock_1_out), .D(d_ff_1_q), .Q(d_ff_2_q), .reset(in_1));  // open: Qn, preset, en
  D_Flip_Flop d_ff_3 (.clk(clock_1_out), .D(d_ff_4_q), .Q(d_ff_3_q), .reset(in_1));  // open: Qn, preset, en
  D_Flip_Flop d_ff_4 (.clk(clock_1_out), .D(d_ff_2_q), .Q(d_ff_4_q), .reset(in_1));  // open: Qn, preset, en
  not not_1 (not_1_out, d_ff_3_q);
endmodule
