// Logisim project projeto.circ as structural Verilog: 5 circuits, main circuit main
module main (
  input  in_1,
  input  in_2,
  input  in_3,
  input  in_4,
  input  in_5
);

  wire \aleatório_1_p1 , \aleatório_1_p2 , \aleatório_1_p3 , check_y_1_out_3, check_y_2_out_3,
       check_y_3_out_3, d_ff_1_q, or_1_out;

  D_Flip_Flop d_ff_1 (.clk(in_2), .D(1'b1), .Q(d_ff_1_q), .reset(in_3));  // open: Qn, preset, en
  // aleatório aleatório_1: pin names not known; wires that end beside it: \aleatório_1_p1 , \aleatório_1_p2 , \aleatório_1_p3 
  LED led_1 (.in(\aleatório_1_p1 ));
  LED led_2 (.in(\aleatório_1_p2 ));
  LED led_3 (.in(\aleatório_1_p3 ));
  check_y check_y_1 (.in_1(\aleatório_1_p1 ), .in_2(in_1), .out_3(check_y_1_out_3));
  check_y check_y_2 (.in_1(\aleatório_1_p2 ), .in_2(in_4), .out_3(check_y_2_out_3));
  check_y check_y_3 (.in_1(\aleatório_1_p3 ), .in_2(in_5), .out_3(check_y_3_out_3));
  or or_1 (or_1_out, check_y_1_out_3, check_y_2_out_3, check_y_3_out_3);
  contador contador_1 (.in_1(or_1_out));  // open: in_2, out_3
endmodule

module contador (
  input  in_1,
  input  in_2,
  output [4:0] out_3
);

  wire [4:0] adder_1_out;

  Adder #(.width(5)) adder_1 (.a(5'b00001), .b(out_3), .out(adder_1_out));  // open: cin, cout
  Register #(.width(5)) register_1 (.D(adder_1_out), .Q(out_3), .clk(in_1), .clr(in_2));  // open: en
  // Probe on adder_1_out
endmodule

module \aleatório  (
  input  in_1,
  input  in_2,
  input  [1:0] in_3,
  input  [1:0] in_4,
  input  [1:0] in_5,
  output out_6,
  output out_7
);

  wire button_1_out, button_2_out, button_3_out, clock_1_out, comparator_1_eq, comparator_1_gt,
       comparator_1_lt, comparator_2_eq, comparator_2_gt, comparator_2_lt, comparator_3_eq, comparator_3_gt,
       comparator_3_lt, d_ff_1_qn, d_ff_2_qn;
  wire [1:0] d_ff_1_q, multiplexer_1_out, multiplexer_2_out, multiplexer_3_out, register_1_q;

  Clock clock_1 (.out(clock_1_out));
  D_Flip_Flop d_ff_1 (
    .clk(clock_1_out), .D(d_ff_1_qn), .Q(d_ff_1_q[0]), .Qn(d_ff_1_qn), .reset(in_1));  // open: preset, en
  D_Flip_Flop d_ff_2 (
    .clk(d_ff_1_qn), .D(d_ff_2_qn), .Q(d_ff_1_q[1]), .Qn(d_ff_2_qn), .reset(in_1));  // open: preset, en
  Register #(.width(2)) register_1 (.D(d_ff_1_q), .Q(register_1_q), .clk(in_2));  // open: en, clr
  Button button_1 (.out(button_1_out));
  Multiplexer #(.width(2), .enable("false")) multiplexer_1 (
    .in1(in_5), .out(multiplexer_1_out), .sel(button_2_out));  // open: in0
  Button button_2 (.out(button_2_out));
  Multiplexer #(.width(2), .enable("false")) multiplexer_2 (
    .in1(in_3), .out(multiplexer_2_out), .sel(button_1_out));  // open: in0
  Multiplexer #(.width(2), .enable("false")) multiplexer_3 (
    .in1(in_4), .out(multiplexer_3_out), .sel(button_3_out));  // open: in0
  Button button_3 (.out(button_3_out));
  Comparator #(.width(2), .mode("unsigned")) comparator_1 (
    .a(register_1_q), .b(multiplexer_2_out), .gt(comparator_1_gt), .eq(comparator_1_eq), .lt(comparator_1_lt));
  Comparator #(.width(2), .mode("unsigned")) comparator_2 (
    .a(register_1_q), .b(multiplexer_3_out), .gt(comparator_2_gt), .eq(comparator_2_eq), .lt(comparator_2_lt));
  Comparator #(.width(2), .mode("unsigned")) comparator_3 (
    .a(register_1_q), .b(multiplexer_1_out), .gt(comparator_3_gt), .eq(comparator_3_eq), .lt(comparator_3_lt));
  or or_1 (out_6, comparator_1_eq, comparator_2_eq, comparator_3_eq);
  or or_2 (out_7, comparator_1_gt, comparator_1_lt, comparator_2_gt, comparator_2_lt, comparator_3_gt, comparator_3_lt);
endmodule

module check_y (
  input  in_1,
  input  in_2,
  output out_3
);

  and and_1 (out_3, in_1, in_2);
endmodule

module check_n (
  input  in_1,
  input  in_2,
  input  in_3,
  output out_4
);

  wire or_1_out;

  and and_1 (out_4, in_1, or_1_out);
  or or_1 (or_1_out, in_2, in_3);
endmodule
