// Logisim project sinaleiro.circ as structural Verilog: 4 circuits, main circuit main
module main (
);

  wire and_1_out, and_2_out, and_3_out, and_4_out, and_5_out, and_6_out, and_7_out, button_1_out,
       clock_1_out, debouncer_1_out_3, not_1_out, not_2_out, or_1_out, or_2_out, q0_q, q0_qn, q1_q, q1_qn,
       reset_out, rg_1_out_3, rg_1_out_4, rg_2_out_3, rg_2_out_4;

  Clock clock_1 (.out(clock_1_out));
  Button reset (.out(reset_out));
  not not_1 (not_1_out, 1'b1);
  not not_2 (not_2_out, debouncer_1_out_3);
  debouncer debouncer_1 (.in_1(clock_1_out), .in_2(button_1_out), .out_3(debouncer_1_out_3));
  Button button_1 (.out(button_1_out));
  D_Flip_Flop q1 (.clk(clock_1_out), .D(or_1_out), .Q(q1_q), .Qn(q1_qn), .reset(reset_out));  // open: preset, en
  D_Flip_Flop q0 (.clk(clock_1_out), .D(or_2_out), .Q(q0_q), .Qn(q0_qn), .reset(reset_out));  // open: preset, en
  and and_1 (and_1_out, 1'b1, debouncer_1_out_3, q1_qn, q0_q);
  and and_2 (and_2_out, not_1_out, q1_q, q0_qn);
  and and_3 (and_3_out, not_2_out, q1_q, q0_qn);
  and and_4 (and_4_out, 1'b1, q1_qn, q0_qn);
  and and_5 (and_5_out, not_2_out, 1'b1, q1_qn);
  and and_6 (and_6_out, not_1_out, q1_qn, q0_q);
  and and_7 (and_7_out, debouncer_1_out_3, 1'b1, q1_q, q0_qn);
  or or_1 (or_1_out, and_1_out, and_2_out, and_3_out);
  or or_2 (or_2_out, and_4_out, and_5_out, and_6_out, and_7_out);
  LED led_1 (.in(rg_1_out_3));
  rg rg_1 (.in_1(q1_qn), .in_2(q0_q), .out_3(rg_1_out_3), .out_4(rg_1_out_4));
  LED led_2 (.in(rg_1_out_4));
  LED led_3 (.in(rg_2_out_3));
  rg rg_2 (.in_1(q1_q), .in_2(q0_qn), .out_3(rg_2_out_3), .out_4(rg_2_out_4));
  LED led_4 (.in(rg_2_out_4));
endmodule

module debouncer (
  input  in_1,
  input  in_2,
  output out_3
);

  wire d_ff_1_q, d_ff_2_qn;

  D_Flip_Flop d_ff_1 (.clk(in_1), .D(in_2), .Q(d_ff_1_q));  // open: Qn, preset, en, reset
  D_Flip_Flop d_ff_2 (.clk(in_1), .D(d_ff_1_q), .Qn(d_ff_2_qn));  // open: Q, preset, en, reset
  and and_1 (out_3, d_ff_2_qn, d_ff_1_q);
endmodule

module rg (
  input  in_1,
  input  in_2,
  output out_3,
  output out_4
);

  wire and_1_out;

  and and_1 (and_1_out, in_1, in_2);
  Demultiplexer demultiplexer_1 (.out0(out_3), .out1(out_4), .in(1'b1), .sel(and_1_out));  // open: en
endmodule

module timer (
  input  in_1,
  input  in_2,
  output out_3
);

  D_Flip_Flop d_ff_1 (.clk(in_1), .D(1'b1), .Q(out_3), .reset(in_2));  // open: Qn, preset, en
endmodule
