// Logisim project tasi.circ as structural Verilog: 5 circuits, main circuit comp-2
module main (
  input  [2:0] A,
  input  [1:0] in_2,
  input  [2:0] B
);

  wire and_1_out, n0to9_1_a_2, n0to9_1_b_2, n0to9_1_c_2, n0to9_1_d_2, n0to9_1_e, n0to9_1_f, n0to9_1_g,
       n01_1_a_2, n01_1_b_2, n01_1_c_2, n01_1_d_2, n01_1_e, n01_1_f, n01_1_g;
  wire [3:0] comp_2_1_out_5, comp_2_2_out_5, comp_2_3_out_5, multiplexer_1_out, multiplexer_2_out;
  wire [4:0] ds_1_out_3, multiplexer_3_out;

  comp_2 comp_2_1 (
    .in_1(A[0]), .in_2(A[1]), .in_3(A[2]), .in_4(1'b0), .out_5(comp_2_1_out_5[0]), .out_6(comp_2_1_out_5[1]),
    .out_7(comp_2_1_out_5[2]), .out_8(comp_2_1_out_5[3]));
  comp_2 comp_2_2 (
    .in_1(B[0]), .in_2(B[1]), .in_3(B[2]), .in_4(1'b0), .out_5(comp_2_2_out_5[0]), .out_6(comp_2_2_out_5[1]),
    .out_7(comp_2_2_out_5[2]), .out_8(comp_2_2_out_5[3]));
  // Probe on multiplexer_1_out
  Multiplexer #(.width(4)) multiplexer_1 (
    .in0({1'b0, A}), .in1(comp_2_1_out_5), .out(multiplexer_1_out), .sel(in_2[1]));  // open: en
  Multiplexer #(.width(4)) multiplexer_2 (
    .in0({1'b0, B}), .in1(comp_2_2_out_5), .out(multiplexer_2_out), .sel(in_2[0]));  // open: en
  // Probe on multiplexer_2_out
  and and_1 (and_1_out, in_2[1], in_2[0]);
  ds ds_1 (.in_1(multiplexer_1_out), .in_2(multiplexer_2_out), .out_3(ds_1_out_3));
  // Probe on ds_1_out_3
  // Probe on {ds_1_out_3[4], comp_2_3_out_5}
  comp_2 comp_2_3 (
    .in_1(ds_1_out_3[0]), .in_2(ds_1_out_3[1]), .in_3(ds_1_out_3[2]), .in_4(ds_1_out_3[3]),
    .out_5(comp_2_3_out_5[0]), .out_6(comp_2_3_out_5[1]), .out_7(comp_2_3_out_5[2]), .out_8(comp_2_3_out_5[3]));
  // Probe on multiplexer_3_out
  Multiplexer #(.width(5)) multiplexer_3 (
    .in0(ds_1_out_3), .in1({ds_1_out_3[4], comp_2_3_out_5}), .out(multiplexer_3_out), .sel(and_1_out));  // open: en
  _0to9 u_0to9_1 (
    .A(multiplexer_3_out[3]), .B(multiplexer_3_out[2]), .C(multiplexer_3_out[1]), .D(multiplexer_3_out[0]),
    .a_2(n0to9_1_a_2), .b_2(n0to9_1_b_2), .c_2(n0to9_1_c_2), .d_2(n0to9_1_d_2), .e(n0to9_1_e), .f(n0to9_1_f),
    .g(n0to9_1_g));
  _01 u_01_1 (
    .A(multiplexer_3_out[3]), .B(multiplexer_3_out[2]), .C(multiplexer_3_out[1]), .D(multiplexer_3_out[0]),
    .a_2(n01_1_a_2), .b_2(n01_1_b_2), .c_2(n01_1_c_2), .d_2(n01_1_d_2), .e(n01_1_e), .f(n01_1_f), .g(n01_1_g));
  _7_Segment_Display u_7_segment_display_1 (.g(multiplexer_3_out[4]));  // open: f, a, b, e, d, c, dp
  _7_Segment_Display u_7_segment_display_2 (
    .g(n01_1_g), .f(n01_1_f), .a(n01_1_a_2), .b(n01_1_b_2), .e(n01_1_e), .d(n01_1_d_2), .c(n01_1_c_2));  // open: dp
  _7_Segment_Display u_7_segment_display_3 (
    .g(n0to9_1_g), .f(n0to9_1_f), .a(n0to9_1_a_2), .b(n0to9_1_b_2), .e(n0to9_1_e), .d(n0to9_1_d_2),
    .c(n0to9_1_c_2));  // open: dp
endmodule

module comp_2 (
  input  in_1,
  input  in_2,
  input  in_3,
  input  in_4,
  output out_5,
  output out_6,
  output out_7,
  output out_8
);

  wire adder_1_cout, adder_2_cout, adder_3_cout, not_1_out, not_2_out, not_3_out, not_4_out;

  not not_1 (not_1_out, in_1);
  not not_2 (not_2_out, in_2);
  not not_3 (not_3_out, in_3);
  not not_4 (not_4_out, in_4);
  Adder #(.width(1)) adder_1 (.a(1'b1), .b(not_1_out), .out(out_5), .cin(1'b0), .cout(adder_1_cout));
  Adder #(.width(1)) adder_2 (.a(adder_1_cout), .b(not_2_out), .out(out_6), .cout(adder_2_cout));  // open: cin
  Adder #(.width(1)) adder_3 (.a(adder_2_cout), .b(not_3_out), .out(out_7), .cout(adder_3_cout));  // open: cin
  Adder #(.width(1)) adder_4 (.a(adder_3_cout), .b(not_4_out), .out(out_8));  // open: cin, cout
endmodule

module ds (
  input  [3:0] in_1,
  input  [3:0] in_2,
  output [4:0] out_3
);

  wire adder_1_cout, adder_2_cout, adder_3_cout, not_1_out, xnor_1_out;
  wire [4:0] adder_1_out;
  wire [4:4] adder_4_cout;

  Adder #(.width(1)) adder_1 (.a(in_1[0]), .b(in_2[0]), .out(adder_1_out[0]), .cin(1'b0), .cout(adder_1_cout));
  Adder #(.width(1)) adder_2 (.a(in_1[1]), .b(in_2[1]), .out(adder_1_out[1]), .cin(adder_1_cout), .cout(adder_2_cout));
  Adder #(.width(1)) adder_3 (.a(in_1[2]), .b(in_2[2]), .out(adder_1_out[2]), .cin(adder_2_cout), .cout(adder_3_cout));
  Adder #(.width(1)) adder_4 (
    .a(in_1[3]), .b(in_2[3]), .out(adder_1_out[4]), .cin(adder_3_cout), .cout(adder_4_cout[4]));
  xnor xnor_1 (xnor_1_out, adder_4_cout[4], adder_3_cout);
  Multiplexer #(.width(5)) multiplexer_1 (
    .in0({{2{adder_1_out[4]}}, adder_1_out[2:0]}), .in1({adder_4_cout[4], adder_1_out[4], adder_1_out[2:0]}),
    .out(out_3), .sel(not_1_out));  // open: en
  not not_1 (not_1_out, xnor_1_out);
  // Probe on out_3
endmodule

module _0to9 (
  input  A,
  input  B,
  input  C,
  input  D,
  output a_2,
  output b_2,
  output c_2,
  output d_2,
  output e,
  output f,
  output g
);

  wire and_1_out, and_2_out, and_3_out, and_4_out, and_5_out, and_6_out, and_7_out, and_8_out, and_9_out,
       and_10_out, and_11_out, and_12_out, and_13_out, and_14_out, and_15_out, and_16_out, and_17_out,
       and_18_out, and_19_out, and_20_out, and_21_out, and_22_out, and_23_out, and_24_out, and_25_out,
       and_26_out, and_27_out, and_28_out, and_29_out, and_30_out, and_31_out, not_1_out, not_2_out,
       not_3_out, not_4_out, not_5_out, not_6_out, not_7_out, not_8_out, not_9_out, not_10_out, not_11_out,
       not_12_out, not_13_out, not_14_out, not_15_out, not_16_out, not_17_out, not_18_out, not_19_out,
       not_20_out, not_21_out, not_22_out, not_23_out, not_24_out, not_25_out, not_26_out, not_27_out,
       not_28_out, not_29_out, not_30_out, not_31_out, not_32_out, not_33_out, not_34_out, not_35_out,
       not_36_out, not_37_out, not_38_out, not_39_out, not_40_out, not_41_out, not_42_out, not_43_out,
       not_44_out, not_45_out;

  not not_1 (not_1_out, B);
  and and_1 (and_1_out, not_1_out, not_2_out);
  not not_2 (not_2_out, D);
  not not_3 (not_3_out, A);
  not not_4 (not_4_out, B);
  and and_2 (and_2_out, not_3_out, not_4_out, C);
  and and_3 (and_3_out, B, D);
  and and_4 (and_4_out, A, not_5_out);
  not not_5 (not_5_out, C);
  not not_6 (not_6_out, B);
  not not_7 (not_7_out, C);
  and and_5 (and_5_out, not_7_out, not_8_out);
  not not_8 (not_8_out, D);
  not not_9 (not_9_out, A);
  and and_6 (and_6_out, not_9_out, C, D);
  and and_7 (and_7_out, A, not_10_out);
  not not_10 (not_10_out, C);
  and and_8 (and_8_out, A, not_11_out);
  not not_11 (not_11_out, D);
  not not_12 (not_12_out, A);
  and and_9 (and_9_out, not_12_out, not_13_out);
  not not_13 (not_13_out, C);
  and and_10 (and_10_out, B, C);
  and and_11 (and_11_out, A, not_14_out);
  not not_14 (not_14_out, B);
  not not_15 (not_15_out, B);
  and and_12 (and_12_out, not_15_out, not_16_out);
  not not_16 (not_16_out, D);
  not not_17 (not_17_out, A);
  and and_13 (and_13_out, not_17_out, not_18_out, C);
  not not_18 (not_18_out, B);
  not not_19 (not_19_out, A);
  and and_14 (and_14_out, not_19_out, C, not_20_out);
  not not_20 (not_20_out, D);
  not not_21 (not_21_out, C);
  and and_15 (and_15_out, B, not_21_out, D);
  and and_16 (and_16_out, A, not_22_out, not_23_out);
  not not_22 (not_22_out, C);
  not not_23 (not_23_out, D);
  and and_17 (and_17_out, A, B, D);
  not not_24 (not_24_out, B);
  and and_18 (and_18_out, not_24_out, not_25_out);
  not not_25 (not_25_out, D);
  not not_26 (not_26_out, A);
  and and_19 (and_19_out, not_26_out, C, not_27_out);
  not not_27 (not_27_out, D);
  and and_20 (and_20_out, A, not_28_out, not_29_out);
  not not_28 (not_28_out, C);
  not not_29 (not_29_out, D);
  not not_30 (not_30_out, A);
  not not_31 (not_31_out, C);
  and and_21 (and_21_out, not_30_out, not_31_out, not_32_out);
  not not_32 (not_32_out, D);
  not not_33 (not_33_out, A);
  and and_22 (and_22_out, not_33_out, B, not_34_out);
  not not_34 (not_34_out, C);
  not not_35 (not_35_out, A);
  and and_23 (and_23_out, not_35_out, B, not_36_out);
  not not_36 (not_36_out, D);
  and and_24 (and_24_out, A, not_37_out, not_38_out);
  not not_37 (not_37_out, B);
  not not_38 (not_38_out, C);
  not not_39 (not_39_out, B);
  and and_25 (and_25_out, A, not_39_out, not_40_out);
  not not_40 (not_40_out, D);
  and and_26 (and_26_out, A, B, C);
  not not_41 (not_41_out, A);
  and and_27 (and_27_out, not_41_out, not_42_out, C);
  not not_42 (not_42_out, B);
  and and_28 (and_28_out, B, not_43_out);
  not not_43 (not_43_out, C);
  and and_29 (and_29_out, B, not_44_out);
  not not_44 (not_44_out, D);
  and and_30 (and_30_out, A, not_45_out);
  not not_45 (not_45_out, C);
  and and_31 (and_31_out, A, B);
  or or_1 (a_2, and_1_out, and_2_out, and_3_out, and_4_out);
  or or_2 (b_2, not_6_out, and_5_out, and_6_out, and_7_out, and_8_out);
  or or_3 (c_2, and_9_out, D, and_10_out, and_11_out);
  or or_4 (e, and_18_out, and_19_out, and_20_out);
  or or_5 (g, and_27_out, and_28_out, and_29_out, and_30_out, and_31_out);
  or or_6 (d_2, and_12_out, and_13_out, and_14_out, and_15_out, and_16_out, and_17_out);
  or or_7 (f, and_21_out, and_22_out, and_23_out, and_24_out, and_25_out, and_26_out);
endmodule

module _01 (
  input  A,
  input  B,
  input  C,
  input  D,
  output a_2,
  output b_2,
  output c_2,
  output d_2,
  output e,
  output f,
  output g
);

  wire and_1_out, and_2_out, and_3_out, and_4_out, not_1_out, not_2_out, not_3_out, not_4_out, not_5_out,
       not_6_out, not_7_out, not_8_out, not_9_out, not_10_out, not_11_out, not_12_out;

  not not_1 (not_1_out, A);
  not not_2 (not_2_out, B);
  and and_1 (and_1_out, not_2_out, not_3_out);
  not not_3 (not_3_out, C);
  not not_4 (not_4_out, A);
  not not_5 (not_5_out, B);
  and and_2 (and_2_out, not_5_out, not_6_out);
  not not_6 (not_6_out, C);
  not not_7 (not_7_out, A);
  not not_8 (not_8_out, B);
  and and_3 (and_3_out, not_8_out, not_9_out);
  not not_9 (not_9_out, C);
  not not_10 (not_10_out, A);
  not not_11 (not_11_out, B);
  and and_4 (and_4_out, not_11_out, not_12_out);
  not not_12 (not_12_out, C);
  or or_1 (a_2, not_1_out, and_1_out);
  or or_2 (d_2, not_4_out, and_2_out);
  or or_3 (e, not_7_out, and_3_out);
  or or_4 (f, not_10_out, and_4_out);

  assign b_2 = 1'b1;
  assign c_2 = 1'b1;
  assign g = 1'b0;
endmodule
