// Logisim project teclado.circ as structural Verilog: 6 circuits, main circuit main
module main (
);

  wire clock_1_out, consonant_1_out_8, consonant_1_out_9, consonant_1_out_10, consonant_1_out_11,
       consonant_1_out_12, consonant_1_out_13, consonant_1_out_14, controlled_buffer_1_out, isvogal_1_x,
       keyboard_1_avail;
  wire [6:0] keyboard_1_data, multiplexer_1_out, numtossd_1_s, vogal_1_s;

  Clock clock_1 (.out(clock_1_out));
  assign controlled_buffer_1_out = keyboard_1_avail ? clock_1_out : 1'bz;  // Controlled_Buffer controlled_buffer_1
  Keyboard keyboard_1 (
    .clk(controlled_buffer_1_out), .avail(keyboard_1_avail), .data(keyboard_1_data));  // open: re, clr
  // Probe on keyboard_1_data
  vogal vogal_1 (
    .a(keyboard_1_data[6]), .b(keyboard_1_data[5]), .c(keyboard_1_data[4]), .d(keyboard_1_data[3]),
    .e(keyboard_1_data[2]), .f(keyboard_1_data[1]), .g(keyboard_1_data[0]), .x(vogal_1_s[6]),
    .y(vogal_1_s[5]), .z(vogal_1_s[4]), .u(vogal_1_s[3]), .v(vogal_1_s[2]), .w(vogal_1_s[1]), .s(vogal_1_s[0]));
  isvogal isvogal_1 (
    .a(keyboard_1_data[6]), .b(keyboard_1_data[5]), .c(keyboard_1_data[4]), .d(keyboard_1_data[3]),
    .e(keyboard_1_data[2]), .f(keyboard_1_data[1]), .g(keyboard_1_data[0]), .x(isvogal_1_x));
  consonant consonant_1 (
    .in_1(keyboard_1_data[6]), .in_2(keyboard_1_data[5]), .in_3(keyboard_1_data[4]),
    .in_4(keyboard_1_data[3]), .in_5(keyboard_1_data[2]), .in_6(keyboard_1_data[1]),
    .in_7(keyboard_1_data[0]), .out_8(consonant_1_out_8), .out_9(consonant_1_out_9),
    .out_10(consonant_1_out_10), .out_11(consonant_1_out_11), .out_12(consonant_1_out_12),
    .out_13(consonant_1_out_13), .out_14(consonant_1_out_14));
  numtoSSD numtossd_1 (
    .a(consonant_1_out_8), .b(consonant_1_out_9), .c(consonant_1_out_10), .d(consonant_1_out_11),
    .e(consonant_1_out_12), .f(consonant_1_out_13), .g(consonant_1_out_14), .x(numtossd_1_s[6]),
    .y(numtossd_1_s[5]), .z(numtossd_1_s[4]), .u(numtossd_1_s[3]), .v(numtossd_1_s[2]), .w(numtossd_1_s[1]),
    .s(numtossd_1_s[0]));
  Multiplexer #(.width(7)) multiplexer_1 (
    .in0(numtossd_1_s), .in1(vogal_1_s), .out(multiplexer_1_out), .sel(isvogal_1_x));  // open: en
  _7_Segment_Display u_7_segment_display_1 (
    .g(multiplexer_1_out[0]), .f(multiplexer_1_out[1]), .a(multiplexer_1_out[6]), .b(multiplexer_1_out[5]),
    .e(multiplexer_1_out[2]), .d(multiplexer_1_out[3]), .c(multiplexer_1_out[4]));  // open: dp
endmodule

module vogal (
  input  a,
  input  b,
  input  c,
  input  d,
  input  e,
  input  f,
  input  g,
  output x,
  output y,
  output z,
  output u,
  output v,
  output w,
  output s
);

  wire and_1_out, and_2_out, and_3_out, and_4_out, and_5_out, not_1_out, not_2_out, not_3_out, not_4_out,
       not_5_out, not_6_out, not_7_out, not_8_out, not_9_out, not_10_out, not_11_out;

  not not_1 (not_1_out, d);
  not not_2 (not_2_out, e);
  not not_3 (not_3_out, c);
  not not_4 (not_4_out, d);
  not not_5 (not_5_out, e);
  not not_6 (not_6_out, d);
  not not_7 (not_7_out, e);
  not not_8 (not_8_out, c);
  not not_9 (not_9_out, f);
  not not_10 (not_10_out, c);
  not not_11 (not_11_out, d);
  and and_1 (and_1_out, not_1_out, not_2_out);
  and and_2 (and_2_out, not_3_out, e);
  and and_3 (and_3_out, not_4_out, not_5_out);
  and and_4 (and_4_out, not_6_out, not_7_out);
  and and_5 (and_5_out, a, b, not_8_out, not_9_out, g);
  and and_6 (s, not_10_out, not_11_out);
  or or_1 (x, and_1_out, and_2_out);
  or or_2 (y, and_3_out, f, c);
  or or_3 (z, and_4_out, f, c);
  or or_4 (w, e, d, and_5_out);

  assign u = e;
  assign v = 1'b1;
endmodule

module consonant (
  input  in_1,
  input  in_2,
  input  in_3,
  input  in_4,
  input  in_5,
  input  in_6,
  input  in_7,
  output out_8,
  output out_9,
  output out_10,
  output out_11,
  output out_12,
  output out_13,
  output out_14
);

  wire adder_1_cout, adder_1_out, adder_2_cout, adder_2_out, adder_3_cout, adder_3_out, adder_4_cout,
       adder_4_out, adder_5_cout, adder_5_out, adder_6_cout, adder_6_out, adder_7_out, adder_8_cout,
       adder_8_out, adder_9_cout, adder_10_cout;

  Adder #(.width(1)) adder_1 (.a(in_1), .b(in_2), .out(adder_1_out), .cin(1'b0), .cout(adder_1_cout));
  Adder #(.width(1)) adder_2 (.a(in_3), .b(in_4), .out(adder_2_out), .cin(1'b0), .cout(adder_2_cout));
  Adder #(.width(1)) adder_3 (.a(in_5), .b(in_6), .out(adder_3_out), .cin(1'b0), .cout(adder_3_cout));
  Adder #(.width(1)) adder_4 (.a(in_7), .b(1'b0), .out(adder_4_out), .cin(1'b0), .cout(adder_4_cout));
  Adder #(.width(1)) adder_5 (
    .a(adder_1_cout), .b(adder_2_cout), .out(adder_5_out), .cin(adder_6_cout), .cout(adder_5_cout));
  Adder #(.width(1)) adder_6 (.a(adder_1_out), .b(adder_2_out), .out(adder_6_out), .cin(1'b0), .cout(adder_6_cout));
  Adder #(.width(1)) adder_7 (.a(adder_3_cout), .b(adder_4_cout), .out(adder_7_out), .cin(adder_8_cout));  // open: cout
  Adder #(.width(1)) adder_8 (.a(adder_3_out), .b(adder_4_out), .out(adder_8_out), .cin(1'b0), .cout(adder_8_cout));
  Adder #(.width(1)) adder_9 (.a(adder_5_out), .b(adder_7_out), .out(out_13), .cin(adder_10_cout), .cout(adder_9_cout));
  Adder #(.width(1)) adder_10 (.a(adder_6_out), .b(adder_8_out), .out(out_14), .cin(1'b0), .cout(adder_10_cout));
  Adder #(.width(1)) adder_11 (.a(adder_5_cout), .b(1'b0), .out(out_12), .cin(adder_9_cout));  // open: cout

  assign out_8 = 1'b0;
  assign out_9 = 1'b0;
  assign out_10 = 1'b0;
  assign out_11 = 1'b0;
endmodule

module isvogal (
  input  a,
  input  b,
  input  c,
  input  d,
  input  e,
  input  f,
  input  g,
  output x
);

  wire and_1_out, and_2_out, and_3_out, not_1_out, not_2_out, not_3_out, not_4_out, not_5_out, not_6_out;

  not not_1 (not_1_out, c);
  not not_2 (not_2_out, e);
  not not_3 (not_3_out, f);
  not not_4 (not_4_out, d);
  not not_5 (not_5_out, f);
  not not_6 (not_6_out, c);
  and and_1 (and_1_out, a, b, not_1_out, not_2_out, not_3_out, g);
  and and_2 (and_2_out, a, b, not_4_out, e, not_5_out, g);
  and and_3 (and_3_out, a, b, not_6_out, d, e, f, g);
  or or_1 (x, and_1_out, and_2_out, and_3_out);
endmodule

module half_adder (
  input  in_1,
  input  in_2,
  output out_3,
  output out_4
);

  xor xor_1 (out_3, in_1, in_2);
  and and_1 (out_4, in_1, in_2);
endmodule

module numtoSSD (
  input  a,
  input  b,
  input  c,
  input  d,
  input  e,
  input  f,
  input  g,
  output x,
  output y,
  output z,
  output u,
  output v,
  output w,
  output s
);

  wire and_1_out, and_2_out, and_3_out, and_4_out, and_5_out, and_6_out, and_7_out, and_8_out, and_9_out,
       and_10_out, and_11_out, and_12_out, and_13_out, and_14_out, and_15_out, and_16_out, not_1_out,
       not_2_out, not_3_out, not_4_out, not_5_out, not_6_out, not_7_out, not_8_out, not_9_out, not_10_out,
       not_11_out, not_12_out, not_13_out, not_14_out;

  and and_1 (and_1_out, e, g);
  not not_1 (not_1_out, e);
  not not_2 (not_2_out, e);
  not not_3 (not_3_out, f);
  not not_4 (not_4_out, g);
  not not_5 (not_5_out, e);
  not not_6 (not_6_out, f);
  not not_7 (not_7_out, g);
  not not_8 (not_8_out, e);
  not not_9 (not_9_out, g);
  not not_10 (not_10_out, f);
  not not_11 (not_11_out, g);
  not not_12 (not_12_out, e);
  not not_13 (not_13_out, g);
  not not_14 (not_14_out, f);
  or or_1 (x, f, and_1_out);
  and and_2 (and_2_out, not_1_out, g);
  and and_3 (and_3_out, not_2_out, f);
  and and_4 (and_4_out, f, g);
  and and_5 (and_5_out, e, not_3_out, not_4_out);
  and and_6 (and_6_out, not_5_out, g);
  and and_7 (and_7_out, not_6_out, g);
  and and_8 (and_8_out, e, not_7_out);
  and and_9 (and_9_out, not_8_out, f);
  and and_10 (and_10_out, f, not_9_out);
  and and_11 (and_11_out, e, not_10_out, g);
  and and_12 (and_12_out, f, not_11_out);
  and and_13 (and_13_out, e, f);
  and and_14 (and_14_out, not_12_out, f);
  and and_15 (and_15_out, f, not_13_out);
  and and_16 (and_16_out, e, not_14_out);
  or or_2 (y, and_2_out, and_3_out, and_4_out, and_5_out);
  or or_3 (z, and_6_out, and_7_out, and_8_out);
  or or_4 (u, and_9_out, and_10_out, and_11_out);
  or or_5 (v, and_12_out, and_13_out);
  or or_6 (s, and_14_out, and_15_out, and_16_out);

  assign w = e;
endmodule
