// Logisim project teste.circ as structural Verilog: 4 circuits, main circuit main
module main (
);

  wire and_1_out, and_2_out, button_1_out, clock_1_out, counter_1_out_3, not_1_out, not_2_out, not_3_out,
       not_4_out, register_1_q, ssd_1_a, ssd_1_b, ssd_1_c, ssd_1_d, ssd_1_e, ssd_1_f, ssd_1_g, ssd_2_a,
       ssd_2_b, ssd_2_c, ssd_2_d, ssd_2_e, ssd_2_f, ssd_2_g;
  wire [3:0] counter_1_out_2, counter_6_1_out_2;

  Clock clock_1 (.out(clock_1_out));
  Register #(.width(1)) register_1 (.D(1'b1), .Q(register_1_q), .clk(button_1_out), .clr(and_2_out));  // open: en
  Button button_1 (.out(button_1_out));
  and and_1 (and_1_out, clock_1_out, register_1_q);
  and and_2 (and_2_out, not_1_out, not_2_out, counter_1_out_3, not_3_out, not_4_out);
  counter_6 counter_6_1 (.in_1(counter_1_out_3), .out_2(counter_6_1_out_2));
  not not_1 (not_1_out, counter_6_1_out_2[3]);
  not not_2 (not_2_out, counter_6_1_out_2[2]);
  not not_3 (not_3_out, counter_6_1_out_2[1]);
  not not_4 (not_4_out, counter_6_1_out_2[0]);
  _7_Segment_Display u_7_segment_display_1 (
    .g(ssd_1_g), .f(ssd_1_f), .a(ssd_1_a), .b(ssd_1_b), .e(ssd_1_e), .d(ssd_1_d), .c(ssd_1_c));  // open: dp
  ssd ssd_1 (
    .in_1(counter_6_1_out_2), .a(ssd_1_a), .b(ssd_1_b), .c(ssd_1_c), .d(ssd_1_d), .e(ssd_1_e), .f(ssd_1_f),
    .g(ssd_1_g));
  _7_Segment_Display u_7_segment_display_2 (
    .g(ssd_2_g), .f(ssd_2_f), .a(ssd_2_a), .b(ssd_2_b), .e(ssd_2_e), .d(ssd_2_d), .c(ssd_2_c));  // open: dp
  ssd ssd_2 (
    .in_1(counter_1_out_2), .a(ssd_2_a), .b(ssd_2_b), .c(ssd_2_c), .d(ssd_2_d), .e(ssd_2_e), .f(ssd_2_f),
    .g(ssd_2_g));
  counter counter_1 (.in_1(and_1_out), .out_2(counter_1_out_2), .out_3(counter_1_out_3));
endmodule

module counter (
  input  in_1,
  output [3:0] out_2,
  output out_3
);

  wire d_ff_1_qn, d_ff_2_qn, d_ff_3_qn, d_ff_4_qn, not_1_out, not_2_out, not_3_out, not_4_out;

  D_Flip_Flop d_ff_1 (.clk(in_1), .D(d_ff_1_qn), .Q(out_2[0]), .Qn(d_ff_1_qn), .preset(out_3));  // open: en, reset
  D_Flip_Flop d_ff_2 (.clk(out_2[0]), .D(d_ff_2_qn), .Q(out_2[1]), .Qn(d_ff_2_qn), .reset(out_3));  // open: preset, en
  and and_1 (out_3, not_1_out, not_2_out, not_3_out, not_4_out);
  D_Flip_Flop d_ff_3 (.clk(out_2[1]), .D(d_ff_3_qn), .Q(out_2[2]), .Qn(d_ff_3_qn), .reset(out_3));  // open: preset, en
  not not_1 (not_1_out, out_2[0]);
  not not_2 (not_2_out, out_2[1]);
  not not_3 (not_3_out, out_2[2]);
  not not_4 (not_4_out, out_2[3]);
  D_Flip_Flop d_ff_4 (.clk(out_2[2]), .D(d_ff_4_qn), .Q(out_2[3]), .Qn(d_ff_4_qn), .preset(out_3));  // open: en, reset
  // Probe on out_2
endmodule

module ssd (
  input  [3:0] in_1,
  output a,
  output b,
  output c,
  output d,
  output e,
  output f,
  output g
);

  wire and_1_out, and_2_out, and_3_out, and_4_out, and_5_out, and_6_out, and_7_out, and_8_out, and_9_out,
       and_10_out, and_11_out, and_12_out, and_13_out, and_14_out, and_15_out, and_16_out, not_1_out,
       not_2_out, not_3_out, not_4_out, not_5_out, not_6_out, not_7_out, not_8_out, not_9_out, not_10_out,
       not_11_out, not_12_out, not_13_out, not_14_out, not_15_out, not_16_out, not_17_out, not_18_out,
       not_19_out, not_20_out, not_21_out;

  not not_1 (not_1_out, in_1[2]);
  and and_1 (and_1_out, not_1_out, not_2_out);
  not not_2 (not_2_out, in_1[0]);
  and and_2 (and_2_out, in_1[2], in_1[0]);
  not not_3 (not_3_out, in_1[2]);
  not not_4 (not_4_out, in_1[1]);
  and and_3 (and_3_out, not_4_out, not_5_out);
  not not_5 (not_5_out, in_1[0]);
  and and_4 (and_4_out, in_1[1], in_1[0]);
  not not_6 (not_6_out, in_1[1]);
  or or_1 (c, not_6_out, in_1[0], in_1[2]);
  not not_7 (not_7_out, in_1[2]);
  and and_5 (and_5_out, not_7_out, not_8_out);
  not not_8 (not_8_out, in_1[0]);
  not not_9 (not_9_out, in_1[2]);
  and and_6 (and_6_out, not_9_out, in_1[1]);
  and and_7 (and_7_out, in_1[1], not_10_out);
  not not_10 (not_10_out, in_1[0]);
  not not_11 (not_11_out, in_1[1]);
  and and_8 (and_8_out, in_1[2], not_11_out, in_1[0]);
  not not_12 (not_12_out, in_1[2]);
  and and_9 (and_9_out, not_12_out, not_13_out);
  not not_13 (not_13_out, in_1[0]);
  and and_10 (and_10_out, in_1[1], not_14_out);
  not not_14 (not_14_out, in_1[0]);
  not not_15 (not_15_out, in_1[1]);
  and and_11 (and_11_out, not_15_out, not_16_out);
  not not_16 (not_16_out, in_1[0]);
  and and_12 (and_12_out, in_1[2], not_17_out);
  not not_17 (not_17_out, in_1[1]);
  and and_13 (and_13_out, in_1[2], not_18_out);
  not not_18 (not_18_out, in_1[0]);
  not not_19 (not_19_out, in_1[2]);
  and and_14 (and_14_out, not_19_out, in_1[1]);
  and and_15 (and_15_out, in_1[2], not_20_out);
  not not_20 (not_20_out, in_1[1]);
  and and_16 (and_16_out, in_1[2], not_21_out);
  not not_21 (not_21_out, in_1[0]);
  or or_2 (a, and_1_out, in_1[1], and_2_out, in_1[3]);
  or or_3 (b, not_3_out, and_3_out, and_4_out);
  or or_4 (d, and_5_out, and_6_out, and_7_out, and_8_out, in_1[3]);
  or or_5 (e, and_9_out, and_10_out);
  or or_6 (f, and_11_out, and_12_out, and_13_out, in_1[3]);
  or or_7 (g, and_14_out, and_15_out, and_16_out, in_1[3]);
endmodule

module counter_6 (
  input  in_1,
  output [3:0] out_2
);

  wire and_1_out, d_ff_1_qn, d_ff_2_qn, d_ff_3_qn, d_ff_4_qn;

  D_Flip_Flop d_ff_1 (.clk(in_1), .D(d_ff_1_qn), .Q(out_2[0]), .Qn(d_ff_1_qn), .preset(and_1_out));  // open: en, reset
  D_Flip_Flop d_ff_2 (
    .clk(out_2[0]), .D(d_ff_2_qn), .Q(out_2[1]), .Qn(d_ff_2_qn), .reset(and_1_out));  // open: preset, en
  and and_1 (and_1_out, out_2[0], out_2[1], out_2[2], out_2[3]);
  D_Flip_Flop d_ff_3 (
    .clk(out_2[1]), .D(d_ff_3_qn), .Q(out_2[2]), .Qn(d_ff_3_qn), .preset(and_1_out));  // open: en, reset
  D_Flip_Flop d_ff_4 (
    .clk(out_2[2]), .D(d_ff_4_qn), .Q(out_2[3]), .Qn(d_ff_4_qn), .reset(and_1_out));  // open: preset, en
  // Probe on out_2
endmodule
