// Logisim project ula.circ as structural Verilog: 8 circuits, main circuit main
module main (
  input  [2:0] A,
  input  [2:0] B,
  input  [1:0] OP
);

  wire not_1_out, zero_nove_1_s, zero_nove_1_u, zero_nove_1_v, zero_nove_1_w, zero_nove_1_x, zero_nove_1_y,
       zero_nove_1_z, zeroum_1_v, zeroum_1_w;
  wire [3:0] soma_1_out_10;
  wire [4:0] multiplexer_1_out, sub_1_out_11, subsoma_1_out_11, subsub_1_out_11;

  soma soma_1 (
    .in_1(A[2]), .in_2(B[2]), .in_3(A[1]), .in_4(B[1]), .in_5(A[0]), .in_6(B[0]), .out_7(soma_1_out_10[3]),
    .out_8(soma_1_out_10[2]), .out_9(soma_1_out_10[1]), .out_10(soma_1_out_10[0]));
  sub sub_1 (
    .in_1(A[2]), .in_2(B[2]), .in_3(A[1]), .in_4(B[1]), .in_5(A[0]), .in_6(B[0]), .out_7(sub_1_out_11[4]),
    .out_8(sub_1_out_11[3]), .out_9(sub_1_out_11[2]), .out_10(sub_1_out_11[1]), .out_11(sub_1_out_11[0]));
  subSoma subsoma_1 (
    .in_1(A[2]), .in_2(B[2]), .in_3(A[1]), .in_4(B[1]), .in_5(A[0]), .in_6(B[0]),
    .out_7(subsoma_1_out_11[4]), .out_8(subsoma_1_out_11[3]), .out_9(subsoma_1_out_11[2]),
    .out_10(subsoma_1_out_11[1]), .out_11(subsoma_1_out_11[0]));
  subSub subsub_1 (
    .in_1(A[2]), .in_2(B[2]), .in_3(A[1]), .in_4(B[1]), .in_5(A[0]), .in_6(B[0]), .out_7(subsub_1_out_11[4]),
    .out_8(subsub_1_out_11[3]), .out_9(subsub_1_out_11[2]), .out_10(subsub_1_out_11[1]),
    .out_11(subsub_1_out_11[0]));
  Multiplexer #(.select(2), .width(5)) multiplexer_1 (
    .in0({1'b1, soma_1_out_10}), .in1(sub_1_out_11), .in2(subsoma_1_out_11), .in3(subsub_1_out_11),
    .out(multiplexer_1_out), .sel(OP));  // open: en
  // Probe on multiplexer_1_out
  not not_1 (not_1_out, multiplexer_1_out[4]);
  zeroum zeroum_1 (
    .a(multiplexer_1_out[3]), .b(multiplexer_1_out[2]), .c(multiplexer_1_out[1]), .d(multiplexer_1_out[0]),
    .v(zeroum_1_v), .w(zeroum_1_w));  // open: x, y, z, u, s
  zero_nove zero_nove_1 (
    .a(multiplexer_1_out[3]), .b(multiplexer_1_out[2]), .c(multiplexer_1_out[1]), .d(multiplexer_1_out[0]),
    .x(zero_nove_1_x), .y(zero_nove_1_y), .z(zero_nove_1_z), .u(zero_nove_1_u), .v(zero_nove_1_v),
    .w(zero_nove_1_w), .s(zero_nove_1_s));
  _7_Segment_Display u_7_segment_display_1 (.g(not_1_out));  // open: f, a, b, e, d, c, dp
  _7_Segment_Display u_7_segment_display_2 (.f(zeroum_1_w), .e(zeroum_1_v));  // open: g, a, b, d, c, dp
  _7_Segment_Display u_7_segment_display_3 (
    .g(zero_nove_1_s), .f(zero_nove_1_w), .a(zero_nove_1_x), .b(zero_nove_1_y), .e(zero_nove_1_v),
    .d(zero_nove_1_u), .c(zero_nove_1_z));  // open: dp
endmodule

module soma (
  input  in_1,
  input  in_2,
  input  in_3,
  input  in_4,
  input  in_5,
  input  in_6,
  output out_7,
  output out_8,
  output out_9,
  output out_10
);

  wire adder_2_cout, adder_3_cout;

  Adder #(.width(1)) adder_1 (.a(in_1), .b(in_2), .out(out_8), .cin(adder_2_cout), .cout(out_7));
  Adder #(.width(1)) adder_2 (.a(in_3), .b(in_4), .out(out_9), .cin(adder_3_cout), .cout(adder_2_cout));
  Adder #(.width(1)) adder_3 (.a(in_5), .b(in_6), .out(out_10), .cin(1'b0), .cout(adder_3_cout));
endmodule

module sub (
  input  in_1,
  input  in_2,
  input  in_3,
  input  in_4,
  input  in_5,
  input  in_6,
  output out_7,
  output out_8,
  output out_9,
  output out_10,
  output out_11
);

  wire comp2_1_out_4, comp2_1_out_5, comp2_1_out_6, nor_1_out, soma_1_out_7;
  wire [2:0] comp2_2_out_6, soma_1_out_10;

  comp2 comp2_1 (
    .in_1(in_2), .in_2(in_4), .in_3(in_6), .out_4(comp2_1_out_4), .out_5(comp2_1_out_5), .out_6(comp2_1_out_6));
  soma soma_1 (
    .in_1(in_1), .in_2(comp2_1_out_4), .in_3(in_3), .in_4(comp2_1_out_5), .in_5(in_5), .in_6(comp2_1_out_6),
    .out_7(soma_1_out_7), .out_8(soma_1_out_10[2]), .out_9(soma_1_out_10[1]), .out_10(soma_1_out_10[0]));
  nor nor_1 (nor_1_out, in_6, in_4, in_2);
  comp2 comp2_2 (
    .in_1(soma_1_out_10[2]), .in_2(soma_1_out_10[1]), .in_3(soma_1_out_10[0]), .out_4(comp2_2_out_6[2]),
    .out_5(comp2_2_out_6[1]), .out_6(comp2_2_out_6[0]));
  Multiplexer #(.width(3)) multiplexer_1 (
    .in0(comp2_2_out_6), .in1(soma_1_out_10), .out({out_9, out_10, out_11}), .sel(out_7));  // open: en
  or or_1 (out_7, soma_1_out_7, nor_1_out);

  assign out_8 = 1'b0;
endmodule

module subSoma (
  input  in_1,
  input  in_2,
  input  in_3,
  input  in_4,
  input  in_5,
  input  in_6,
  output out_7,
  output out_8,
  output out_9,
  output out_10,
  output out_11
);

  wire comp2_1_out_4, comp2_1_out_5, comp2_1_out_6, nor_1_out, soma_1_out_7;
  wire [2:0] comp2_2_out_6, soma_1_out_10;

  comp2 comp2_1 (
    .in_1(in_1), .in_2(in_3), .in_3(in_5), .out_4(comp2_1_out_4), .out_5(comp2_1_out_5), .out_6(comp2_1_out_6));
  nor nor_1 (nor_1_out, in_1, in_3, in_5, in_5);
  soma soma_1 (
    .in_1(comp2_1_out_4), .in_2(in_2), .in_3(comp2_1_out_5), .in_4(in_4), .in_5(comp2_1_out_6), .in_6(in_6),
    .out_7(soma_1_out_7), .out_8(soma_1_out_10[2]), .out_9(soma_1_out_10[1]), .out_10(soma_1_out_10[0]));
  comp2 comp2_2 (
    .in_1(soma_1_out_10[2]), .in_2(soma_1_out_10[1]), .in_3(soma_1_out_10[0]), .out_4(comp2_2_out_6[2]),
    .out_5(comp2_2_out_6[1]), .out_6(comp2_2_out_6[0]));
  or or_1 (out_7, soma_1_out_7, nor_1_out);
  Multiplexer #(.width(3)) multiplexer_1 (
    .in0(comp2_2_out_6), .in1(soma_1_out_10), .out({out_9, out_10, out_11}), .sel(out_7));  // open: en

  assign out_8 = 1'b0;
endmodule

module subSub (
  input  in_1,
  input  in_2,
  input  in_3,
  input  in_4,
  input  in_5,
  input  in_6,
  output out_7,
  output out_8,
  output out_9,
  output out_10,
  output out_11
);

  soma soma_1 (
    .in_1(in_1), .in_2(in_2), .in_3(in_3), .in_4(in_4), .in_5(in_5), .in_6(in_6), .out_7(out_8),
    .out_8(out_9), .out_9(out_10), .out_10(out_11));
  nor nor_1 (out_7, out_8, out_9, out_11, out_10);
endmodule

module comp2 (
  input  in_1,
  input  in_2,
  input  in_3,
  output out_4,
  output out_5,
  output out_6
);

  wire adder_2_cout, adder_3_cout, not_1_out, not_2_out, not_3_out;

  not not_1 (not_1_out, in_1);
  not not_2 (not_2_out, in_2);
  not not_3 (not_3_out, in_3);
  Adder #(.width(1)) adder_1 (.a(1'b0), .b(not_1_out), .out(out_4), .cin(adder_2_cout));  // open: cout
  Adder #(.width(1)) adder_2 (.a(1'b0), .b(not_2_out), .out(out_5), .cin(adder_3_cout), .cout(adder_2_cout));
  Adder #(.width(1)) adder_3 (.a(1'b1), .b(not_3_out), .out(out_6), .cin(1'b0), .cout(adder_3_cout));
endmodule

module zeroum (
  input  a,
  input  b,
  input  c,
  input  d,
  output x,
  output y,
  output z,
  output u,
  output v,
  output w,
  output s
);

  wire and_1_out, and_2_out, and_3_out, and_4_out;

  and and_1 (and_1_out, a, c);
  and and_2 (and_2_out, a, b);
  and and_3 (and_3_out, a, c);
  and and_4 (and_4_out, a, b);
  or or_1 (v, and_1_out, and_2_out);
  or or_2 (w, and_3_out, and_4_out);

  assign s = 1'b0;
  assign u = 1'b0;
  assign x = 1'b0;
  assign y = 1'b0;
  assign z = 1'b0;
endmodule

module zero_nove (
  input  a,
  input  b,
  input  c,
  input  d,
  output x,
  output y,
  output z,
  output u,
  output v,
  output w,
  output s
);

  wire and_1_out, and_2_out, and_3_out, and_4_out, and_5_out, and_6_out, and_7_out, and_8_out, and_9_out,
       and_10_out, and_11_out, and_12_out, and_13_out, and_14_out, and_15_out, and_16_out, and_17_out,
       and_18_out, and_19_out, and_20_out, and_21_out, and_22_out, and_23_out, and_24_out, and_25_out,
       and_26_out, and_27_out, and_28_out, and_29_out, and_30_out, and_31_out, and_32_out, and_33_out,
       and_34_out, not_1_out, not_2_out, not_3_out, not_4_out, not_5_out, not_6_out, not_7_out, not_8_out,
       not_9_out, not_10_out, not_11_out, not_12_out, not_13_out, not_14_out, not_15_out, not_16_out,
       not_17_out, not_18_out, not_19_out, not_20_out, not_21_out, not_22_out, not_23_out, not_24_out,
       not_25_out, not_26_out, not_27_out, not_28_out, not_29_out, not_30_out, not_31_out, not_32_out,
       not_33_out, not_34_out, not_35_out, not_36_out, not_37_out, not_38_out, not_39_out, not_40_out,
       not_41_out, not_42_out, not_43_out, not_44_out, not_45_out, not_46_out;

  not not_1 (not_1_out, a);
  not not_2 (not_2_out, b);
  and and_1 (and_1_out, not_1_out, not_2_out, c);
  and and_2 (and_2_out, b, d);
  not not_3 (not_3_out, b);
  and and_3 (and_3_out, a, not_3_out, not_4_out);
  not not_4 (not_4_out, d);
  and and_4 (and_4_out, a, not_5_out);
  not not_5 (not_5_out, c);
  not not_6 (not_6_out, a);
  and and_5 (and_5_out, not_6_out, not_7_out, c);
  not not_7 (not_7_out, b);
  not not_8 (not_8_out, a);
  and and_6 (and_6_out, not_8_out, c, d);
  and and_7 (and_7_out, b, not_9_out, not_10_out);
  not not_9 (not_9_out, c);
  not not_10 (not_10_out, d);
  and and_8 (and_8_out, a, not_11_out);
  not not_11 (not_11_out, c);
  and and_9 (and_9_out, a, not_12_out);
  not not_12 (not_12_out, d);
  not not_13 (not_13_out, a);
  and and_10 (and_10_out, not_13_out, c, d);
  not not_14 (not_14_out, a);
  and and_11 (and_11_out, not_14_out, b);
  and and_12 (and_12_out, b, d);
  not not_15 (not_15_out, b);
  and and_13 (and_13_out, a, not_15_out, not_16_out);
  not not_16 (not_16_out, c);
  and and_14 (and_14_out, a, c, not_17_out);
  not not_17 (not_17_out, d);
  not not_18 (not_18_out, a);
  and and_15 (and_15_out, not_18_out, not_19_out, c);
  not not_19 (not_19_out, b);
  not not_20 (not_20_out, a);
  and and_16 (and_16_out, not_20_out, c, not_21_out);
  not not_21 (not_21_out, d);
  not not_22 (not_22_out, c);
  and and_17 (and_17_out, b, not_22_out, d);
  and and_18 (and_18_out, a, not_23_out, not_24_out);
  not not_23 (not_23_out, b);
  not not_24 (not_24_out, d);
  and and_19 (and_19_out, a, not_25_out, not_26_out);
  not not_25 (not_25_out, c);
  not not_26 (not_26_out, d);
  and and_20 (and_20_out, a, b, d);
  not not_27 (not_27_out, a);
  not not_28 (not_28_out, b);
  not not_29 (not_29_out, c);
  not not_30 (not_30_out, a);
  not not_31 (not_31_out, d);
  not not_32 (not_32_out, c);
  not not_33 (not_33_out, d);
  not not_34 (not_34_out, b);
  not not_35 (not_35_out, a);
  and and_21 (and_21_out, not_35_out, not_36_out, d);
  not not_36 (not_36_out, c);
  not not_37 (not_37_out, a);
  and and_22 (and_22_out, not_37_out, b, not_38_out);
  not not_38 (not_38_out, c);
  not not_39 (not_39_out, a);
  and and_23 (and_23_out, not_39_out, b, not_40_out);
  not not_40 (not_40_out, d);
  and and_24 (and_24_out, a, not_41_out);
  not not_41 (not_41_out, b);
  and and_25 (and_25_out, a, c);
  not not_42 (not_42_out, a);
  and and_26 (and_26_out, not_42_out, not_43_out, c);
  not not_43 (not_43_out, b);
  and and_27 (and_27_out, b, not_44_out);
  not not_44 (not_44_out, c);
  and and_28 (and_28_out, b, not_45_out);
  not not_45 (not_45_out, d);
  and and_29 (and_29_out, a, not_46_out);
  not not_46 (not_46_out, c);
  and and_30 (and_30_out, a, b);
  or or_1 (x, and_1_out, and_2_out, and_3_out, and_4_out);
  or or_2 (y, and_5_out, and_6_out, and_7_out, and_8_out, and_9_out);
  or or_3 (z, and_10_out, and_11_out, and_12_out, and_13_out, and_14_out);
  and and_31 (and_31_out, not_27_out, not_28_out, not_29_out, d);
  and and_32 (and_32_out, not_30_out, c, not_31_out);
  and and_33 (and_33_out, a, not_32_out, not_33_out);
  and and_34 (and_34_out, a, not_34_out, c);
  or or_4 (w, and_21_out, and_22_out, and_23_out, and_24_out, and_25_out);
  or or_5 (s, and_26_out, and_27_out, and_28_out, and_29_out, and_30_out);
  or or_6 (u, and_15_out, and_16_out, and_17_out, and_18_out, and_19_out, and_20_out);
  or or_7 (v, and_31_out, and_32_out, and_33_out, and_34_out);
endmodule
